// Logisim project Memory_Copier.circ as structural Verilog: 1 circuit, main circuit main
module main (
);

  wire CLK, clock_1_out, clock_2_out, CNT, d_ff_1_q, d_ff_1_qn, d_ff_2_q, ds1813_1_p2, LE, lvc161_1_p8,
       lvc161_2_p8, lvc161_4_p8, lvc161_5_p8, lvc161_6_p8, lvc161_7_p8, nand_1_out, nand_2_out, not_1_out,
       not_6_out, or_1_out, or_2_out, PEB, pull_resistor_3_node, pull_resistor_4_node, pull_resistor_5_node,
       pull_resistor_6_node, pull_resistor_7_node, pull_resistor_8_node, pull_resistor_9_node,
       pull_resistor_10_node, pull_resistor_11_node, pull_resistor_13_node, pull_resistor_14_node,
       pull_resistor_15_node, pull_resistor_16_node, pull_resistor_17_node, pull_resistor_18_node,
       pull_resistor_19_node, pull_resistor_20_node, pull_resistor_21_node, READ_B, TRANSPARENCY_B, WRITE_B1,
       WRITE_B2, WRITE_ENABLE;
  wire [2:2] pull_resistor_12_node;
  wire [3:0] lvc161_1_p7, lvc161_2_p7, lvc161_3_p6, lvc161_4_p7, lvc161_5_p7, lvc161_6_p7, lvc161_7_p7,
       lvc161_8_p7, lvc161_9_p7;
  wire [7:0] lvc138_1_p5, lvc573_1_p4, ram_1_data;
  wire [23:0] DESTINATION_ADDRESS;

  Clock clock_1 (.out(clock_1_out));
  Pull_Resistor pull_resistor_1 (.node(TRANSPARENCY_B));
  Pull_Resistor #(.pull(1)) pull_resistor_2 (.node(CNT));
  // DS1813 ds1813_1: pin names not known; wires that end beside it: clock_1_out, ds1813_1_p2, ds1813_1_p2
  Clock clock_2 (.out(clock_2_out));
  not not_1 (not_1_out, clock_2_out);
  D_Flip_Flop d_ff_1 (.clk(clock_2_out), .D(ds1813_1_p2), .Q(d_ff_1_q), .Qn(d_ff_1_qn));  // open: preset, reset
  D_Flip_Flop d_ff_2 (.clk(not_1_out), .D(d_ff_1_qn), .Q(d_ff_2_q));  // open: Qn, preset, reset
  and and_1 (LE, d_ff_1_q, d_ff_2_q);
  Pull_Resistor #(.pull(1)) pull_resistor_3 (.node(pull_resistor_3_node));
  Pull_Resistor #(.pull(1)) pull_resistor_4 (.node(pull_resistor_4_node));
  Pull_Resistor #(.pull(1)) pull_resistor_5 (.node(pull_resistor_5_node));
  Pull_Resistor #(.pull(1)) pull_resistor_6 (.node(pull_resistor_6_node));
  not not_2 (PEB, LE);
  Pull_Resistor #(.pull(1)) pull_resistor_7 (.node(pull_resistor_7_node));
  // LVC161 lvc161_1: pin names not known; wires that end beside it: pull_resistor_3_node, PEB, 4'b0111, CLK, pull_resistor_4_node, CNT, lvc161_1_p7, lvc161_1_p8
  // LVC161 lvc161_2: pin names not known; wires that end beside it: pull_resistor_5_node, PEB, 4'b0000, CLK, pull_resistor_6_node, CNT, lvc161_2_p7, lvc161_2_p8
  or or_1 (or_1_out, WRITE_B1, WRITE_B2);
  // Probe on DESTINATION_ADDRESS
  RAM #(.addrWidth(24), .databus("bidir"), .enables("line"), .trigger("high"), .\type ("nonvolatile")) ram_1 (
    .addr(DESTINATION_ADDRESS), .data(ram_1_data));  // open: we, oe, clk
  // NOT_Gate not_3 has open pins: in=READ_B, out=open
  // NOT_Gate not_4 has open pins: in=or_1_out, out=open
  // NOT_Gate not_5 has open pins: in=pull_resistor_8_node, out=open
  Pull_Resistor pull_resistor_8 (.node(pull_resistor_8_node));
  // LVC161 lvc161_3: pin names not known; wires that end beside it: ds1813_1_p2, pull_resistor_7_node, clock_2_out, pull_resistor_7_node, CNT, lvc161_3_p6
  Pull_Resistor #(.pull(1)) pull_resistor_9 (.node(pull_resistor_9_node));
  Pull_Resistor #(.pull(1)) pull_resistor_10 (.node(pull_resistor_10_node));
  // LVC161 lvc161_4: pin names not known; wires that end beside it: pull_resistor_9_node, PEB, 4'b1010, CLK, lvc161_1_p8, CNT, lvc161_4_p7, lvc161_4_p8
  // LVC161 lvc161_5: pin names not known; wires that end beside it: pull_resistor_10_node, PEB, 4'b0000, CLK, lvc161_2_p8, CNT, lvc161_5_p7, lvc161_5_p8
  Pull_Resistor pull_resistor_11 (.node(pull_resistor_11_node));
  Pull_Resistor pull_resistor_12 (.node(pull_resistor_12_node[2]));
  Pull_Resistor #(.pull(1)) pull_resistor_13 (.node(pull_resistor_13_node));
  Pull_Resistor #(.pull(1)) pull_resistor_14 (.node(pull_resistor_14_node));
  Pull_Resistor #(.pull(1)) pull_resistor_15 (.node(pull_resistor_15_node));
  // LVC138 lvc138_1: pin names not known; wires that end beside it: pull_resistor_11_node, pull_resistor_11_node, {pull_resistor_12_node[2], lvc161_3_p6[1:0]}, pull_resistor_13_node, {lvc138_1_p5[7:3], WRITE_B1, lvc138_1_p5[1:0]}
  // LVC161 lvc161_6: pin names not known; wires that end beside it: pull_resistor_14_node, PEB, 4'b0011, CLK, lvc161_4_p8, CNT, lvc161_6_p7, lvc161_6_p8
  // LVC161 lvc161_7: pin names not known; wires that end beside it: pull_resistor_15_node, PEB, 4'b0000, CLK, lvc161_5_p8, CNT, lvc161_7_p7, lvc161_7_p8
  Pull_Resistor pull_resistor_16 (.node(pull_resistor_16_node));
  not not_6 (not_6_out, READ_B);
  // LVC573 lvc573_1: pin names not known; wires that end beside it: pull_resistor_16_node, ram_1_data, not_6_out, lvc573_1_p4
  and and_2 (READ_B, lvc138_1_p5[0], lvc138_1_p5[1]);
  not not_7 (WRITE_ENABLE, lvc138_1_p5[1]);
  not not_8 (CLK, lvc138_1_p5[3]);
  Pull_Resistor #(.pull(1)) pull_resistor_17 (.node(pull_resistor_17_node));
  Pull_Resistor #(.pull(1)) pull_resistor_18 (.node(pull_resistor_18_node));
  // Probe on lvc573_1_p4
  Pull_Resistor pull_resistor_19 (.node(pull_resistor_19_node));
  // LVC161 lvc161_8: pin names not known; wires that end beside it: pull_resistor_17_node, PEB, 4'b1111, CLK, lvc161_6_p8, CNT, lvc161_8_p7
  // LVC161 lvc161_9: pin names not known; wires that end beside it: pull_resistor_18_node, PEB, 4'b0110, CLK, lvc161_7_p8, CNT, lvc161_9_p7
  // LVC4245 lvc4245_1: pin names not known; wires that end beside it: WRITE_B1, lvc573_1_p4, pull_resistor_19_node, ram_1_data
  nand nand_1 (nand_1_out, ~lvc573_1_p4[0], ~lvc573_1_p4[1], ~lvc573_1_p4[2], ~lvc573_1_p4[3]);  // NAND_Gate
  nand nand_2 (nand_2_out, ~lvc573_1_p4[4], ~lvc573_1_p4[5], ~lvc573_1_p4[6], ~lvc573_1_p4[7]);  // NAND_Gate
  or or_2 (or_2_out, nand_1_out, nand_2_out, TRANSPARENCY_B);
  Pull_Resistor pull_resistor_20 (.node(pull_resistor_20_node));
  Pull_Resistor pull_resistor_21 (.node(pull_resistor_21_node));
  D_Flip_Flop d_ff_3 (.clk(WRITE_ENABLE), .D(or_2_out), .Qn(WRITE_B2));  // open: Q, preset, reset
  // LVC573 lvc573_2: pin names not known; wires that end beside it: READ_B, 8'h1, LE, DESTINATION_ADDRESS[23:16]
  // LVC164245 lvc164245_1: pin names not known; wires that end beside it: READ_B, READ_B, {lvc161_8_p7, lvc161_6_p7}, pull_resistor_20_node, {lvc161_4_p7, lvc161_1_p7}, pull_resistor_20_node, DESTINATION_ADDRESS[15:8], DESTINATION_ADDRESS[7:0]
  // LVC573 lvc573_3: pin names not known; wires that end beside it: WRITE_B1, {8{1'b0}}, LE, DESTINATION_ADDRESS[23:16]
  // LVC164245 lvc164245_2: pin names not known; wires that end beside it: WRITE_B1, WRITE_B1, {lvc161_9_p7, lvc161_7_p7}, pull_resistor_21_node, {lvc161_5_p7, lvc161_2_p7}, pull_resistor_21_node, DESTINATION_ADDRESS[15:8], DESTINATION_ADDRESS[7:0]

  // Other names for the same wires on the sheet: SOURCE_ADDRESS[23:0] = DESTINATION_ADDRESS
endmodule
