// Logisim project Test.circ as structural Verilog: 1 circuit, main circuit main
module main (
);

  wire PHI2, w65c02s_1_p1, w65c02s_1_p2, w65c02s_1_p3, w65c02s_1_p4, w65c02s_1_p5, w65c02s_1_p6,
       w65c02s_1_p13, w65c02s_1_p14, w65c02s_1_p16, w65c02s_1_p17, w65c02s_1_p19, w65c816s_1_p1,
       w65c816s_1_p2, w65c816s_1_p3, w65c816s_1_p4, w65c816s_1_p5, w65c816s_1_p6, w65c816s_1_p7,
       w65c816s_1_p16, w65c816s_1_p17, w65c816s_1_p18, w65c816s_1_p19, w65c816s_1_p20, w65c816s_1_p21,
       w65c816s_1_p22, w65c816s_1_p23;
  wire [23:0] Tick_Count;

  Clock clock_1 (.out(PHI2));
  Counter #(.max('hffffff), .width(24)) counter_1 (.Q(Tick_Count), .clk(PHI2));  // open: load, D, count, carry, up, clr
  // W65C02S w65c02s_1: pin names not known; wires that end beside it: w65c02s_1_p1, w65c02s_1_p2, w65c02s_1_p3, w65c02s_1_p4, w65c02s_1_p5, w65c02s_1_p6, w65c02s_1_p1, w65c02s_1_p2, w65c02s_1_p3, w65c02s_1_p4, w65c02s_1_p5, w65c02s_1_p6, w65c02s_1_p13, w65c02s_1_p14, PHI2, w65c02s_1_p16, w65c02s_1_p17, {8{1'b1}}, w65c02s_1_p19, w65c02s_1_p13, w65c02s_1_p14, w65c02s_1_p16, w65c02s_1_p17, w65c02s_1_p19
  // W65C816S w65c816s_1: pin names not known; wires that end beside it: w65c816s_1_p1, w65c816s_1_p2, w65c816s_1_p3, w65c816s_1_p4, w65c816s_1_p5, w65c816s_1_p6, w65c816s_1_p7, w65c816s_1_p1, w65c816s_1_p2, w65c816s_1_p3, w65c816s_1_p4, PHI2, w65c816s_1_p5, w65c816s_1_p6, w65c816s_1_p7, w65c816s_1_p16, w65c816s_1_p17, w65c816s_1_p18, w65c816s_1_p19, w65c816s_1_p20, w65c816s_1_p21, w65c816s_1_p22, w65c816s_1_p23, w65c816s_1_p16, w65c816s_1_p18, w65c816s_1_p19, w65c816s_1_p20, w65c816s_1_p21, w65c816s_1_p22, w65c816s_1_p23
  // Probe on w65c816s_1_p17
endmodule
