// Logisim project demo.circ as structural Verilog: 1 circuit, main circuit main
module main (
);

  wire and_1_out, and_2_out, and_3_out, clock_1_out, counter_1_carry, dipswitch_1_p1, dipswitch_1_p2,
       dipswitch_1_p3, dipswitch_1_p4, dipswitch_1_p5, dipswitch_1_p6, dipswitch_1_p7, dipswitch_1_p8,
       not_1_out, not_4_out, not_5_out, not_6_out, or_1_out, pull_resistor_2_node, w65c816s_1_p10,
       w65c816s_1_p11, w65c816s_1_p12, w65c816s_1_p13, w65c816s_1_p14, w65c816s_1_p15;
  wire [7:0] w65c816s_1_p8, w65c816s_1_p9;
  wire [15:0] w65c816s_1_p7;

  Clock clock_1 (.out(clock_1_out));
  Counter #(.max('h1), .width(1)) counter_1 (
    .carry(counter_1_carry), .clk(and_1_out));  // open: load, D, count, Q, up, clr
  and and_1 (and_1_out, clock_1_out, not_1_out);
  not not_1 (not_1_out, counter_1_carry);
  // DipSwitch #(.number(3)) dipswitch_1: pin names not known; wires that end beside it: dipswitch_1_p1, dipswitch_1_p2, dipswitch_1_p3, dipswitch_1_p4, dipswitch_1_p5, dipswitch_1_p6, dipswitch_1_p7, dipswitch_1_p8
  not not_2 (dipswitch_1_p7, dipswitch_1_p1);
  not not_3 (dipswitch_1_p8, dipswitch_1_p2);
  not not_4 (not_4_out, dipswitch_1_p3);
  // W65C816S w65c816s_1: pin names not known; wires that end beside it: not_4_out, counter_1_carry, clock_1_out, dipswitch_1_p4, dipswitch_1_p5, dipswitch_1_p6, w65c816s_1_p7, w65c816s_1_p8, w65c816s_1_p9, w65c816s_1_p10, w65c816s_1_p11, w65c816s_1_p12, w65c816s_1_p13, w65c816s_1_p14, w65c816s_1_p15, w65c816s_1_p11, w65c816s_1_p14
  // Probe on w65c816s_1_p8
  Register #(.trigger("high")) register_1 (.D(w65c816s_1_p8), .clk(clock_1_out));  // open: en, Q, clr
  Pull_Resistor #(.pull(1)) pull_resistor_1 (.node(w65c816s_1_p15));
  not not_5 (not_5_out, clock_1_out);
  not not_6 (not_6_out, w65c816s_1_p10);
  or or_1 (or_1_out, w65c816s_1_p12, w65c816s_1_p13);
  and and_2 (and_2_out, clock_1_out, or_1_out, w65c816s_1_p10);
  and and_3 (and_3_out, not_5_out, not_6_out);
  // Probe on w65c816s_1_p9
  // Probe on w65c816s_1_p7
  RAM #(.addrWidth(16), .databus("bidir"), .enables("line"), .trigger("high"), .\type ("nonvolatile")) ram_1 (
    .addr(w65c816s_1_p7), .data(w65c816s_1_p9));  // open: we, oe, clk
  Pull_Resistor #(.pull(1)) pull_resistor_2 (.node(pull_resistor_2_node));
endmodule
