// Logisim project demo2.circ as structural Verilog: 1 circuit, main circuit main
module main (
  input  in_1
);

  wire not_1_out, not_2_out, not_3_out, PHI2, pull_resistor_1_node, pull_resistor_3_node, RWB,
       w65c816s_1_p10, w65c816s_1_p12;
  wire [7:0] A0_7, A8_15, BA0_7, D;

  Clock clock_1 (.out(PHI2));
  Pull_Resistor #(.pull(1)) pull_resistor_1 (.node(pull_resistor_1_node));
  not not_1 (not_1_out, RWB);
  // W65C816S w65c816s_1: pin names not known; wires that end beside it: pull_resistor_1_node, pull_resistor_1_node, pull_resistor_1_node, in_1, PHI2, not_1_out, RWB, PHI2, {A8_15, A0_7}, w65c816s_1_p10, RWB, w65c816s_1_p12
  RAM #(.addrWidth(24), .databus("bidir"), .enables("line"), .trigger("high"), .\type ("nonvolatile")) ram_1 (
    .addr({BA0_7, A8_15, A0_7}), .data(D));  // open: we, oe, clk
  Pull_Resistor #(.pull(1)) pull_resistor_2 (.node(w65c816s_1_p12));
  Pull_Resistor pull_resistor_3 (.node(pull_resistor_3_node));
  not not_2 (not_2_out, PHI2);
  not not_3 (not_3_out, PHI2);
  // LVC573 lvc573_1: pin names not known; wires that end beside it: pull_resistor_3_node, w65c816s_1_p10, not_2_out, BA0_7
  // LVC4245 lvc4245_1: pin names not known; wires that end beside it: not_3_out, w65c816s_1_p10, RWB, D
endmodule
